# Fritzing sketch RGBLED Lamp Common Anode No Resistors (saved by Fritzing 0.9.0b)
breadboards: 1

parts:
  Part1 = Spark Core (v1.0)
  RGB_LED_(Common_Anode) = RGB LED (com. anode, rbg) [package="5 mm [THT]"]

nets:
  N1: Part1.A5, RGB_LED_(Common_Anode).green_cathode
  N2: Part1.A6, RGB_LED_(Common_Anode).blue_cathode
  N3: Part1.A7, RGB_LED_(Common_Anode).red_cathode
  N4: Part1.3V3*, RGB_LED_(Common_Anode).common_anode
