# Fritzing sketch RGBLED Lamp Common Anode (saved by Fritzing 0.9.0b)
breadboards: 1

parts:
  Part1 = Spark Core (v1.0)
  R1 = Resistor [tolerance=±5% resistance=330 package=THT]
  R2 = Resistor [tolerance=±5% resistance=330 package=THT]
  R3 = Resistor [tolerance=±5% resistance=330 package=THT]
  RGB_LED_(Common_Anode) = RGB LED (com. anode, rbg) [package="5 mm [THT]"]

nets:
  N1: Part1.A5, R3.Pin_1
  N2: Part1.A6, R2.Pin_1
  N3: Part1.A7, R1.Pin_1
  N4: Part1.3V3*, RGB_LED_(Common_Anode).common_anode
  N5: R1.Pin_0, RGB_LED_(Common_Anode).red_cathode
  N6: R2.Pin_0, RGB_LED_(Common_Anode).blue_cathode
  N7: R3.Pin_0, RGB_LED_(Common_Anode).green_cathode
