# Fritzing sketch RGBLED Lamp Common Cathode No Resistors (saved by Fritzing 0.9.0b)
breadboards: 1

parts:
  Part1 = Spark Core (v1.0)
  RGB_LED_(Common_Cathode) = RGB LED (com. cathode, rbg) [package="5 mm [THT]"]

nets:
  N1: Part1.A5, RGB_LED_(Common_Cathode).green_anode
  N2: Part1.A6, RGB_LED_(Common_Cathode).blue_anode
  N3: Part1.A7, RGB_LED_(Common_Cathode).red_anode
  N4: Part1.GND, RGB_LED_(Common_Cathode).common_cathode
