# Fritzing sketch RGBLED Lamp Common Cathode (saved by Fritzing 0.9.0b)
breadboards: 1

parts:
  Part1 = Spark Core (v1.0)
  RGB_LED_(Common_Cathode) = RGB LED (com. cathode, rbg) [package="5 mm [THT]"]
  R1 = Resistor [tolerance=±5% resistance=330 package=THT]
  R2 = Resistor [tolerance=±5% resistance=330 package=THT]
  R3 = Resistor [tolerance=±5% resistance=330 package=THT]

nets:
  N1: Part1.A5, R3.Pin_1
  N2: Part1.A6, R2.Pin_1
  N3: Part1.A7, R1.Pin_1
  N4: Part1.GND, RGB_LED_(Common_Cathode).common_cathode
  N5: RGB_LED_(Common_Cathode).red_anode, R1.Pin_0
  N6: RGB_LED_(Common_Cathode).blue_anode, R2.Pin_0
  N7: RGB_LED_(Common_Cathode).green_anode, R3.Pin_0
